# Fritzing sketch RoombaPong (saved by Fritzing 0.9.8b)

parts:
  Part1 = Arduino Uno (Rev3)
  U1 = ESP8266 WiFi Module [part_number=ESP8266]
  R1 = Resistor [tolerance=±5% resistance=10k package="0402 [SMD]"]
  R2 = Resistor [tolerance=±5% power=0.25 resistance=1k package=THT]
  R3 = Resistor [tolerance=±5% power=0.25 resistance=1k package=THT]
  M1 = RioRand LM2596

nets:
  N1: Part1.D2, R2.Pin_0
  N2: Part1.D3_PWM, U1.TXD
  N3: Part1.3V3, R1.Pin_0
  GND: Part1.GND, U1.GND, M1.Pin_3
  N4: Part1.VIN, M1.Pin_4
  N5: U1.VCC, R1.Pin_1
  N6: R2.Pin_1, R3.Pin_0

notes:
  TX
  3V
  RX
  DC 7-21 TO 5V
  or UBEC
  WARNING
  Arduino Vin can take 7V-20V
  Roomba Vpwr can reach 21V when charging

custom parts:
  ESP8266 WiFi Module: Generic WiFi Module based on the ESP8266 with onboard PCB antenna and UART communications
