# Fritzing sketch UselessMachine (saved by Fritzing 0.9.3b)
breadboards: 1

parts:
  Arduino2 = Arduino Uno (Rev3)
  Part1 = Arduino MP3 Player Shield  # not connected
  J2 = Basic Servo
  J3 = Basic Servo
  Part2 = Breakout Board for Electret Microphone
  NEOPIXEL1 = Neopixel Strip -- Black (60/m)
  Power_plug1 = Power plug
  R1 = Resistor [tolerance=±5% resistance=470 package=THT]
  R2 = Resistor [tolerance=±5% resistance=1k package=THT]
  JP1 = RCA [package=rca_lock]  # not connected

nets:
  N1: Arduino2.A0, Part2.AUD
  N2: Arduino2.D9_PWM, R1.Pin_1
  N3: Arduino2.D10_PWM/SS, J3.pulse
  N4: Arduino2.D11_PWM/MOSI, J2.pulse
  GND: Arduino2.GND, J2.gnd, J3.gnd, Part2.GND, NEOPIXEL1.GND, Power_plug1.GND
  N5: Arduino2.D7, R2.Pin_0
  3V3: Arduino2.3V3, Part2.VCC
  VCC: J2.vcc, J3.vcc, NEOPIXEL1.DI, Power_plug1.VCC
  N6: R1.Pin_0, R2.Pin_1

notes:
  HAL 9000 Useless Machine
  Servos and Leds connected to external power
  Microphone connected to 3.3V
  external power 5V 3Amp
  video
  RCA TV Out
  video sync
  LEDs not in use.
  Replaced with TV Out
  Microphone
  recommended to connect to 3.3v

custom parts:
  Neopixel Strip -- Black (60/m): Neopixel Strip, Black, 60 pixels per meter.
